// Logisim project COMILESTONE2.circ as structural Verilog: 2 circuits, main circuit main
module main (
  input  in_1,
  input  in_2,
  input  in_3,
  input  [2:0] in_4,
  input  in_5,
  input  in_6,
  input  in_7,
  input  [2:0] in_8,
  input  in_9,
  input  in_10,
  output out_11
);

  wire undriven, undriven_2, undriven_3, undriven_4;
  wire [6:0] AR_q, bit_extender_1_out;
  wire [15:0] AC_q, alu_1_ac_output, bit_extender_2_out, DR_q, multiplexer_1_out, ram_1_data, register_1_q,
       register_2_q, TR_q;

  Bit_Extender #(.in_width(16), .out_width(7)) bit_extender_1 (.in(multiplexer_1_out), .out(bit_extender_1_out));
  Register #(.width(7)) AR (.D(bit_extender_1_out), .en(undriven), .Q(AR_q));  // open: clk, clr
  Register #(.width(16)) TR (.D(multiplexer_1_out), .en(undriven_2), .Q(TR_q));  // open: clk, clr
  Register #(.width(16)) DR (.D(multiplexer_1_out), .en(undriven_3), .Q(DR_q));  // open: clk, clr
  Register #(.width(16)) AC (.D(alu_1_ac_output), .en(undriven_4), .Q(AC_q));  // open: clk, clr
  Register #(.width(16)) register_1 (.D(multiplexer_1_out), .en(in_9), .Q(register_1_q));  // open: clk, clr
  Register #(.width(16)) register_2 (.D(multiplexer_1_out), .en(in_10), .Q(register_2_q));  // open: clk, clr
  RAM #(.addrWidth(7), .dataWidth(16), .bus("separate")) ram_1 (
    .addr(AR_q), .din(multiplexer_1_out), .data(ram_1_data), .str(in_1), .ld(in_2));  // open: sel, clk, clr
  assign bit_extender_2_out = {{9{1'b0}}, AR_q};  // Bit_Extender bit_extender_2
  ALU alu_1 (.A(DR_q), .B(AC_q), .in_3(in_8), .E(out_11), .AC_Output(alu_1_ac_output));
  Multiplexer #(.select(3), .width(16)) multiplexer_1 (
    .in0(ram_1_data), .in1(bit_extender_2_out), .in2(TR_q), .in3(DR_q), .in4(AC_q), .in5(register_1_q),
    .in6(register_2_q), .out(multiplexer_1_out), .sel(in_4));  // open: in7, en

  // Notes on the sheet:
  //   PC
  //   IR
endmodule

module ALU (
  input  [15:0] A,
  input  [15:0] B,
  input  [2:0] in_3,
  output E,
  output [15:0] AC_Output
);

  wire adder_1_cout, adder_2_cout, subtractor_1_bout;
  wire [15:0] adder_1_out, adder_2_out, and_1_out, or_1_out, subtractor_1_out, xor_1_out;

  Adder #(.width(16)) adder_1 (.a(A), .b(B), .out(adder_1_out), .cin(1'b0), .cout(adder_1_cout));
  Subtractor #(.width(16)) subtractor_1 (.a(A), .b(B), .out(subtractor_1_out), .bin(1'b0), .bout(subtractor_1_bout));
  assign and_1_out = A & B;  // AND_Gate and_1, 16 bits wide
  assign or_1_out = A | B;  // OR_Gate or_1, 16 bits wide
  assign xor_1_out = A ^ B;  // XOR_Gate xor_1, 16 bits wide
  Adder #(.width(16)) adder_2 (.a(A), .b({16{1'b0}}), .out(adder_2_out), .cin(1'b1), .cout(adder_2_cout));
  or or_2 (E, adder_1_cout, subtractor_1_bout, adder_2_cout);
  Multiplexer #(.select(3), .width(16)) multiplexer_1 (
    .in1(adder_1_out), .in2(subtractor_1_out), .in3(A), .in4(and_1_out), .in5(or_1_out), .in6(xor_1_out),
    .in7(adder_2_out), .out(AC_Output), .sel(in_3));  // open: in0, en
endmodule
